# Fritzing sketch MH_board_v4 (saved by Fritzing 0.8.3b)
breadboards: 1

parts:
  DIN1 = DIN-5 jack (MIDI) [package=THT]
  Bauteil1 = Arduino Mega 2560 (Rev3)
  R1 = Resistor [tolerance=±5% resistance=220 package=THT]
  S1 = Pushbutton [package="[THT]"]
  S2 = Pushbutton [package="[THT]"]
  R11 = Resistor [tolerance=±5% resistance=220 package=THT]
  LED1 = LED - 5mm [color="Red (633nm)" package="5 mm [THT]"]
  LED2 = LED - 5mm [color="Red (633nm)" package="5 mm [THT]"]
  R12 = Resistor [tolerance=±5% resistance=220 package=THT]
  R13 = Resistor [tolerance=±5% resistance=220 package=THT]

nets:
  N1: DIN1.5, R11.Pin_1
  N2: DIN1.2, Bauteil1.GND, S1.Pin_3, S1.Pin_4, S2.Pin_3, S2.Pin_4, LED1.cathode, LED2.cathode
  N3: DIN1.4, R1.Pin_0
  N4: Bauteil1.5V, R1.Pin_1
  N5: Bauteil1.D1_TX0, R11.Pin_0
  N6: Bauteil1.D2_PWM, S1.Pin_1, S1.Pin_2
  N7: Bauteil1.D3_PWM, S2.Pin_1, S2.Pin_2
  N8: Bauteil1.D32, R12.Pin_1
  N9: Bauteil1.D35, R13.Pin_1
  N10: LED1.anode, R12.Pin_0
  N11: LED2.anode, R13.Pin_0
